// Logisim project EP3Final.circ as structural Verilog: 10 circuits, main circuit main
module main (
  input  [7:0] in_1,
  input  reset_pin,
  input  Reset_PC
);

  wire AC_igual_zero, AC_maior_zero, AC_menor_zero, ClkF, clock_1_out, clock_2_out, clock_3_out, clock_4_out,
       d_ff_1_qn, desvia, guarda_em_AC, guarda_em_EE, imprimir_EE, ler, ler_de_EE, not_1_out, OP, or_2_out,
       or_3_out, parar, Reset, ULA_no_AC, verifica;
  wire [3:0] instrucao;
  wire [7:0] AC, demultiplexer_1_out1, EE, Endereco, Entrada_ram, PCout, R, RAM_In, V_AC, V_EE;
  wire [15:0] controlled_buffer_2_out, demultiplexer_1_out0, RAM_Out;
  wire [15:8] IR_q;

  Clock clock_1 (.out(clock_1_out));
  Register u_AC (.D(AC), .en(guarda_em_AC), .clk(clock_2_out), .Q(V_AC), .clr(Reset));
  Clock clock_2 (.out(clock_2_out));
  RAM #(.asyncread("true"), .dataWidth(16)) ram_1 (
    .addr(Endereco), .we(guarda_em_EE), .oe(ler_de_EE), .clk(clock_1_out), .din({{8{1'b0}}, RAM_In}),
    .dout(RAM_Out));
  Demultiplexer #(.width(16)) demultiplexer_1 (
    .out0(demultiplexer_1_out0), .out1({demultiplexer_1_out1, V_EE}), .in(RAM_Out), .sel(guarda_em_AC));
  assign Entrada_ram = not_1_out ? V_AC : 8'bz;  // Controlled_Buffer controlled_buffer_1
  not not_1 (not_1_out, ler);
  Multiplexer #(.width(8)) multiplexer_1 (.in0(Entrada_ram), .in1(in_1), .out(RAM_In), .sel(ler));
  Register #(.width(16)) IR (.D(demultiplexer_1_out0), .clk(clock_3_out), .Q({IR_q, EE}), .clr(Reset));  // open: en
  Clock clock_3 (.out(clock_3_out));
  Multiplexer #(.width(8)) multiplexer_2 (.in0(V_EE), .in1(R), .out(AC), .sel(ULA_no_AC));
  Multiplexer #(.width(4)) multiplexer_3 (.in0(IR_q[11:8]), .in1(4'b0000), .out(instrucao), .sel(ClkF));
  Clock clock_4 (.out(clock_4_out));
  assign controlled_buffer_2_out = imprimir_EE ? RAM_Out : 16'bz;  // Controlled_Buffer controlled_buffer_2
  or or_1 (Reset, reset_pin, parar);
  Hex_Digit_Display hex_digit_display_1 (.value(controlled_buffer_2_out[15:12]));  // open: dp
  D_Flip_Flop d_ff_1 (.D(d_ff_1_qn), .clk(clock_4_out), .Q(ClkF), .Qn(d_ff_1_qn));  // open: preset, reset
  Hex_Digit_Display hex_digit_display_2 (.value(controlled_buffer_2_out[11:8]));  // open: dp
  Hex_Digit_Display hex_digit_display_3 (.value(controlled_buffer_2_out[7:4]));  // open: dp
  Hex_Digit_Display hex_digit_display_4 (.value(controlled_buffer_2_out[3:0]));  // open: dp
  or or_2 (or_2_out, Reset_PC, Reset);
  Counter PC (.clr(or_2_out), .load(desvia), .up(1'b1), .clk(ClkF), .D(EE), .Q(PCout));  // open: count, carry
  or or_3 (or_3_out, verifica, ClkF);
  Multiplexer #(.width(8)) multiplexer_4 (.in0(EE), .in1(PCout), .out(Endereco), .sel(or_3_out));
  ULA ula_1 (
    .OP(OP), .A(V_AC), .B(V_EE), .R(R), .c3(AC_igual_zero), .c4(AC_maior_zero), .c5(AC_menor_zero));  // open: overflow_com_sinal, overflow_sem_sinal, c0, c1, c2
  UC uc_1 (
    .instrucao(instrucao), .AC_maior_zero(AC_maior_zero), .AC_igual_zero(AC_igual_zero),
    .AC_menor_zero(AC_menor_zero), .verifica(verifica), .ULA_no_AC(ULA_no_AC), .guarda_em_AC(guarda_em_AC),
    .ler(ler), .desvia(desvia), .ler_de_EE(ler_de_EE), .guarda_em_EE(guarda_em_EE), .OP(OP),
    .imprimir_EE(imprimir_EE), .parar(parar));

  // Notes on the sheet:
  //   Entrada do usuario
  //   Laís Nuto Rossman - Nº USP: 12547274
  //    Mariana Tiemi Silva Misu  - Nº USP: 12542842 
  //   RAM
  //   OBS: Para evitar erros no funcionamento do programa, favor comece seu programa com um comando do tipo 00xx ou resete manualmente algumas vezes antes.
  //   RAM- responsável pelo funcionamento do programa, 
  //   e como saída o valor lido, caso M2 esteja ligado, no endereço
  //    guardando em seus endereços de memória as instruções que serão executadas.
  //   Para ela utilizamos a RAM já pronta do LOGISIM que tem como entrada o endereço a ser observado,
  //    a opção de leitura ou escrita, um clock, um valor de entrada (que será o valor escrito caso M3 esteja ligado),
  //   Clock
  //   caso a instrução seja ligada, essa libera o buffer controlado e ativa os painéis de 
  //   Display hexadecimal, mostrando a saída da RAM atual
  //   O reset é automático, não usa clock, quando a instrução indicada é a 09. 
  //   Também fizemos um pin de reset manual para facilitar a reiniciação do programa
  //   que tem como função fazer o controle de qual será 
  //   PC- é um contador, utilizamos uma versão já pronta do LOGISIM, 
  //   o próximo endereço de memória analisado pela RAM, considerando possíveis instruções e desvios
endmodule

module UC (
  input  [3:0] instrucao,
  input  AC_maior_zero,
  input  AC_igual_zero,
  input  AC_menor_zero,
  output verifica,
  output ULA_no_AC,
  output guarda_em_AC,
  output ler,
  output desvia,
  output ler_de_EE,
  output guarda_em_EE,
  output OP,
  output imprimir_EE,
  output parar
);

  wire and_1_out, and_2_out, and_3_out, i0, i1, i2, i3, i5, i6, i10, i11, i13, i15, or_2_out;

  Decoder #(.select(4)) decoder_1 (
    .out0(i0), .out1(i1), .out2(i2), .out3(i3), .out4(OP), .out5(i5), .out6(i6), .out7(ler),
    .out8(imprimir_EE), .out9(parar), .out10(i10), .out11(i11), .out13(i13), .out15(i15), .sel(instrucao));  // open: out12, out14, en
  and and_1 (and_1_out, i11, AC_maior_zero);
  and and_2 (and_2_out, i13, AC_igual_zero);
  and and_3 (and_3_out, i15, AC_menor_zero);
  or or_1 (desvia, i10, and_1_out, and_2_out, and_3_out);
  or or_2 (or_2_out, i1, i2, i3, OP, i6, i5, ler, parar, imprimir_EE);
  nor nor_1 (ler_de_EE, ler, i2);
  not not_1 (verifica, or_2_out);
  not not_2 (guarda_em_EE, ler_de_EE);
  or or_3 (ULA_no_AC, i1, i3, OP);
  or or_4 (guarda_em_AC, i3, OP);

  // Other names for the same wires on the sheet: i4 = OP; i7 = ler; i8 = imprimir_EE; i9 = parar
endmodule

module ULA (
  input  OP,
  input  [7:0] A,
  input  [7:0] B,
  output [7:0] R,
  output overflow_com_sinal,
  output overflow_sem_sinal,
  output c0,
  output c1,
  output c2,
  output c3,
  output c4,
  output c5
);

  somador somador_1 (
    .op(OP), .a0(A[0]), .b0(B[0]), .a1(A[1]), .b1(B[1]), .a2(A[2]), .b2(B[2]), .a3(A[3]), .b3(B[3]),
    .a4(A[4]), .b4(B[4]), .a5(A[5]), .b5(B[5]), .a6(A[6]), .b6(B[6]), .a7(A[7]), .b7(B[7]), .out_18(R[0]),
    .out_19(R[1]), .out_20(R[2]), .out_21(R[3]), .out_22(R[4]), .out_23(R[5]), .out_24(R[6]), .out_25(R[7]),
    .overflow_com_sinal(overflow_com_sinal), .overflow_sem_sinal(overflow_sem_sinal));
  Comparador comparador_1 (
    .a0(A[0]), .b0(B[0]), .a1(A[1]), .b1(B[1]), .a2(A[2]), .b2(B[2]), .a3(A[3]), .b3(B[3]), .a4(A[4]),
    .b4(B[4]), .a5(A[5]), .b5(B[5]), .a6(A[6]), .b6(B[6]), .a7(A[7]), .b7(B[7]), .maiorSS(c0), .menorSS(c1),
    .Igual(c2), .igualzero(c3), .maiorCS(c4), .menorCS(c5));
endmodule

module somador (
  input  op,
  input  a0,
  input  b0,
  input  a1,
  input  b1,
  input  a2,
  input  b2,
  input  a3,
  input  b3,
  input  a4,
  input  b4,
  input  a5,
  input  b5,
  input  a6,
  input  b6,
  input  a7,
  input  b7,
  output out_18,
  output out_19,
  output out_20,
  output out_21,
  output out_22,
  output out_23,
  output out_24,
  output out_25,
  output overflow_com_sinal,
  output overflow_sem_sinal
);

  wire somabits_1_carryout, somabits_2_carryout, somabits_3_carryout, somabits_4_carryout,
       somabits_5_carryout, somabits_6_carryout, somabits_7_carryout, somabits_8_carryout, xor_1_out,
       xor_2_out, xor_3_out, xor_4_out, xor_5_out, xor_6_out, xor_7_out, xor_8_out;

  xor xor_1 (xor_1_out, b0, op);
  xor xor_2 (xor_2_out, b1, op);
  xor xor_3 (xor_3_out, b2, op);
  xor xor_4 (xor_4_out, b3, op);
  xor xor_5 (xor_5_out, b4, op);
  xor xor_6 (xor_6_out, b5, op);
  xor xor_7 (xor_7_out, b6, op);
  xor xor_8 (xor_8_out, b7, op);
  somabits somabits_1 (.cin(op), .a(a0), .b(xor_1_out), .s(out_18), .carryout(somabits_1_carryout));
  somabits somabits_2 (.cin(somabits_1_carryout), .a(a1), .b(xor_2_out), .s(out_19), .carryout(somabits_2_carryout));
  somabits somabits_3 (.cin(somabits_2_carryout), .a(a2), .b(xor_3_out), .s(out_20), .carryout(somabits_3_carryout));
  somabits somabits_4 (.cin(somabits_3_carryout), .a(a3), .b(xor_4_out), .s(out_21), .carryout(somabits_4_carryout));
  somabits somabits_5 (.cin(somabits_4_carryout), .a(a4), .b(xor_5_out), .s(out_22), .carryout(somabits_5_carryout));
  somabits somabits_6 (.cin(somabits_5_carryout), .a(a5), .b(xor_6_out), .s(out_23), .carryout(somabits_6_carryout));
  somabits somabits_7 (.cin(somabits_6_carryout), .a(a6), .b(xor_7_out), .s(out_24), .carryout(somabits_7_carryout));
  somabits somabits_8 (.cin(somabits_7_carryout), .a(a7), .b(xor_8_out), .s(out_25), .carryout(somabits_8_carryout));
  xor xor_9 (overflow_com_sinal, somabits_7_carryout, somabits_8_carryout);
  xor xor_10 (overflow_sem_sinal, somabits_8_carryout, op);
endmodule

module somabits (
  input  cin,
  input  a,
  input  b,
  output s,
  output carryout
);

  wire and_1_out, and_2_out, xor_1_out;

  xor xor_1 (xor_1_out, a, b);
  and and_1 (and_1_out, cin, xor_1_out);
  and and_2 (and_2_out, b, a);
  xor xor_2 (s, cin, xor_1_out);
  or or_1 (carryout, and_1_out, and_2_out);
endmodule

module Comparador (
  input  a0,
  input  b0,
  input  a1,
  input  b1,
  input  a2,
  input  b2,
  input  a3,
  input  b3,
  input  a4,
  input  b4,
  input  a5,
  input  b5,
  input  a6,
  input  b6,
  input  a7,
  input  b7,
  output maiorSS,
  output menorSS,
  output Igual,
  output igualzero,
  output maiorCS,
  output menorCS
);

  wire xor_1_out;

  AmaiorB amaiorb_1 (
    .a0(a0), .b0(b0), .a1(a1), .b1(b1), .a2(a2), .b2(b2), .a3(a3), .b3(b3), .a4(a4), .b4(b4), .a5(a5),
    .b5(b5), .a6(a6), .b6(b6), .a7(a7), .b7(b7), .out_17(maiorSS));
  AmenorB amenorb_1 (
    .a0(a0), .b0(b0), .a1(a1), .b1(b1), .a2(a2), .b2(b2), .a3(a3), .b3(b3), .a4(a4), .b4(b4), .a5(a5),
    .b5(b5), .a6(a6), .b6(b6), .a7(a7), .b7(b7), .out_17(menorSS));
  AigualB aigualb_1 (
    .a0(a0), .b0(b0), .a1(a1), .b1(b1), .a2(a2), .b2(b2), .a3(a3), .b3(b3), .a4(a4), .b4(b4), .a5(a5),
    .b5(b5), .a6(a6), .b6(b6), .a7(a7), .b7(b7), .out_17(Igual));
  Aigualzero aigualzero_1 (.a0(a0), .a1(a1), .a2(a2), .a3(a3), .a4(a4), .a5(a5), .a6(a6), .a7(a7), .out_9(igualzero));
  xor xor_1 (xor_1_out, a7, b7);
  xor xor_2 (maiorCS, xor_1_out, maiorSS);
  xor xor_3 (menorCS, menorSS, xor_1_out);
endmodule

module AmenorB (
  input  a0,
  input  b0,
  input  a1,
  input  b1,
  input  a2,
  input  b2,
  input  a3,
  input  b3,
  input  a4,
  input  b4,
  input  a5,
  input  b5,
  input  a6,
  input  b6,
  input  a7,
  input  b7,
  output out_17
);

  wire and_1_out, and_2_out, and_3_out, and_4_out, and_5_out, and_6_out, and_7_out, and_8_out, and_9_out,
       and_10_out, and_11_out, and_12_out, and_13_out, and_14_out, and_15_out, not_1_out, not_2_out,
       not_3_out, not_4_out, not_5_out, not_6_out, not_7_out, not_8_out, not_9_out, not_10_out, not_11_out,
       not_12_out, not_13_out, not_14_out, not_15_out, or_1_out, or_2_out, or_3_out, or_4_out, or_5_out,
       or_6_out, xor_1_out, xor_2_out, xor_3_out, xor_4_out, xor_5_out, xor_6_out, xor_7_out;

  not not_1 (not_1_out, a0);
  xor xor_1 (xor_1_out, b1, a1);
  not not_2 (not_2_out, a1);
  xor xor_2 (xor_2_out, b2, a2);
  not not_3 (not_3_out, a2);
  xor xor_3 (xor_3_out, b3, a3);
  not not_4 (not_4_out, a3);
  xor xor_4 (xor_4_out, b4, a4);
  not not_5 (not_5_out, a4);
  xor xor_5 (xor_5_out, b5, a5);
  not not_6 (not_6_out, a5);
  xor xor_6 (xor_6_out, b6, a6);
  not not_7 (not_7_out, a6);
  xor xor_7 (xor_7_out, b7, a7);
  not not_8 (not_8_out, a7);
  and and_1 (and_1_out, not_1_out, b0);
  not not_9 (not_9_out, xor_1_out);
  and and_2 (and_2_out, not_2_out, b1);
  not not_10 (not_10_out, xor_2_out);
  and and_3 (and_3_out, not_3_out, b2);
  not not_11 (not_11_out, xor_3_out);
  and and_4 (and_4_out, not_4_out, b3);
  not not_12 (not_12_out, xor_4_out);
  and and_5 (and_5_out, not_5_out, b4);
  not not_13 (not_13_out, xor_5_out);
  and and_6 (and_6_out, not_6_out, b5);
  not not_14 (not_14_out, xor_6_out);
  and and_7 (and_7_out, not_7_out, b6);
  not not_15 (not_15_out, xor_7_out);
  and and_8 (and_8_out, not_8_out, b7);
  and and_9 (and_9_out, and_1_out, not_9_out);
  or or_1 (or_1_out, and_9_out, and_2_out);
  and and_10 (and_10_out, or_1_out, not_10_out);
  or or_2 (or_2_out, and_10_out, and_3_out);
  and and_11 (and_11_out, or_2_out, not_11_out);
  or or_3 (or_3_out, and_11_out, and_4_out);
  and and_12 (and_12_out, or_3_out, not_12_out);
  or or_4 (or_4_out, and_12_out, and_5_out);
  and and_13 (and_13_out, or_4_out, not_13_out);
  or or_5 (or_5_out, and_13_out, and_6_out);
  and and_14 (and_14_out, or_5_out, not_14_out);
  or or_6 (or_6_out, and_14_out, and_7_out);
  and and_15 (and_15_out, or_6_out, not_15_out);
  or or_7 (out_17, and_15_out, and_8_out);
endmodule

module AmaiorB (
  input  a0,
  input  b0,
  input  a1,
  input  b1,
  input  a2,
  input  b2,
  input  a3,
  input  b3,
  input  a4,
  input  b4,
  input  a5,
  input  b5,
  input  a6,
  input  b6,
  input  a7,
  input  b7,
  output out_17
);

  wire and_1_out, and_2_out, and_3_out, and_4_out, and_5_out, and_6_out, and_7_out, and_8_out, and_9_out,
       and_10_out, and_11_out, and_12_out, and_13_out, and_14_out, and_15_out, not_1_out, not_2_out,
       not_3_out, not_4_out, not_5_out, not_6_out, not_7_out, not_8_out, not_9_out, not_10_out, not_11_out,
       not_12_out, not_13_out, not_14_out, not_15_out, or_1_out, or_2_out, or_3_out, or_4_out, or_5_out,
       or_6_out, xor_1_out, xor_2_out, xor_3_out, xor_4_out, xor_5_out, xor_6_out, xor_7_out;

  not not_1 (not_1_out, b0);
  not not_2 (not_2_out, b1);
  not not_3 (not_3_out, b4);
  not not_4 (not_4_out, b5);
  not not_5 (not_5_out, b6);
  not not_6 (not_6_out, b7);
  xor xor_1 (xor_1_out, b1, a1);
  xor xor_2 (xor_2_out, b2, a2);
  not not_7 (not_7_out, b2);
  xor xor_3 (xor_3_out, b3, a3);
  not not_8 (not_8_out, b3);
  xor xor_4 (xor_4_out, b4, a4);
  xor xor_5 (xor_5_out, b5, a5);
  xor xor_6 (xor_6_out, b6, a6);
  xor xor_7 (xor_7_out, b7, a7);
  and and_1 (and_1_out, a0, not_1_out);
  not not_9 (not_9_out, xor_1_out);
  and and_2 (and_2_out, a1, not_2_out);
  not not_10 (not_10_out, xor_2_out);
  and and_3 (and_3_out, a2, not_7_out);
  not not_11 (not_11_out, xor_3_out);
  and and_4 (and_4_out, a3, not_8_out);
  not not_12 (not_12_out, xor_4_out);
  and and_5 (and_5_out, a4, not_3_out);
  not not_13 (not_13_out, xor_5_out);
  and and_6 (and_6_out, a5, not_4_out);
  not not_14 (not_14_out, xor_6_out);
  and and_7 (and_7_out, a6, not_5_out);
  not not_15 (not_15_out, xor_7_out);
  and and_8 (and_8_out, a7, not_6_out);
  and and_9 (and_9_out, and_1_out, not_9_out);
  or or_1 (or_1_out, and_9_out, and_2_out);
  and and_10 (and_10_out, or_1_out, not_10_out);
  or or_2 (or_2_out, and_10_out, and_3_out);
  and and_11 (and_11_out, or_2_out, not_11_out);
  or or_3 (or_3_out, and_11_out, and_4_out);
  and and_12 (and_12_out, or_3_out, not_12_out);
  or or_4 (or_4_out, and_12_out, and_5_out);
  and and_13 (and_13_out, or_4_out, not_13_out);
  or or_5 (or_5_out, and_13_out, and_6_out);
  and and_14 (and_14_out, or_5_out, not_14_out);
  or or_6 (or_6_out, and_14_out, and_7_out);
  and and_15 (and_15_out, or_6_out, not_15_out);
  or or_7 (out_17, and_15_out, and_8_out);
endmodule

module AigualB (
  input  a0,
  input  b0,
  input  a1,
  input  b1,
  input  a2,
  input  b2,
  input  a3,
  input  b3,
  input  a4,
  input  b4,
  input  a5,
  input  b5,
  input  a6,
  input  b6,
  input  a7,
  input  b7,
  output out_17
);

  wire and_1_out, and_2_out, and_3_out, and_4_out, and_5_out, and_6_out, not_1_out, not_2_out, not_3_out,
       not_4_out, not_5_out, not_6_out, not_7_out, not_8_out, xor_1_out, xor_2_out, xor_3_out, xor_4_out,
       xor_5_out, xor_6_out, xor_7_out, xor_8_out;

  xor xor_1 (xor_1_out, a0, b0);
  xor xor_2 (xor_2_out, a1, b1);
  xor xor_3 (xor_3_out, a2, b2);
  xor xor_4 (xor_4_out, a3, b3);
  xor xor_5 (xor_5_out, a4, b4);
  xor xor_6 (xor_6_out, a5, b5);
  xor xor_7 (xor_7_out, a6, b6);
  xor xor_8 (xor_8_out, a7, b7);
  not not_1 (not_1_out, xor_1_out);
  not not_2 (not_2_out, xor_2_out);
  not not_3 (not_3_out, xor_3_out);
  not not_4 (not_4_out, xor_4_out);
  not not_5 (not_5_out, xor_5_out);
  not not_6 (not_6_out, xor_6_out);
  not not_7 (not_7_out, xor_7_out);
  not not_8 (not_8_out, xor_8_out);
  and and_1 (and_1_out, not_1_out, not_2_out);
  and and_2 (and_2_out, not_3_out, not_4_out);
  and and_3 (and_3_out, not_5_out, not_6_out);
  and and_4 (and_4_out, not_7_out, not_8_out);
  and and_5 (and_5_out, and_1_out, and_2_out);
  and and_6 (and_6_out, and_3_out, and_4_out);
  and and_7 (out_17, and_5_out, and_6_out);
endmodule

module Aigualzero (
  input  a0,
  input  a1,
  input  a2,
  input  a3,
  input  a4,
  input  a5,
  input  a6,
  input  a7,
  output out_9
);

  wire or_1_out, or_2_out, or_3_out, or_4_out, or_5_out, or_6_out;

  or or_1 (or_1_out, a0, a1);
  or or_2 (or_2_out, a2, a3);
  or or_3 (or_3_out, a4, a5);
  or or_4 (or_4_out, a6, a7);
  or or_5 (or_5_out, or_1_out, or_2_out);
  or or_6 (or_6_out, or_3_out, or_4_out);
  nor nor_1 (out_9, or_5_out, or_6_out);
endmodule
